// Logisim project sketch_16x.circ as structural Verilog
module CPU (
);

  wire [3:0] rom_1_instruction, rom_1_instruction_2, rom_1_instruction_3, rom_1_instruction_4;

  ROM rom_1 (.Instruction({rom_1_instruction_4, rom_1_instruction_3, rom_1_instruction_2, rom_1_instruction}));  // open: Address, jump, clk, clr
  Control_Logic control_logic_1 ();
  RAM ram_1 ();
  ALU alu_1 ();
endmodule

module ROM (
  input  [15:0] Address,
  input  jump,
  input  clk,
  input  clr,
  output [15:0] Instruction
);

  wire [15:0] adder_1_out, multiplexer_1_out, PC_q;

  Multiplexer #(.width(16)) multiplexer_1 (
    .in0(adder_1_out), .in1(Address), .out(multiplexer_1_out), .sel(jump));  // open: en
  Register #(.width(16)) PC (.D(multiplexer_1_out), .Q(PC_q), .clk(clk), .clr(clr));  // open: en
  Adder #(.width(16)) adder_1 (.a(16'h1), .b(PC_q), .out(adder_1_out));  // open: cin, cout
  ROM_part #(.addrWidth(16), .dataWidth(16)) rom_1 (.addr(PC_q), .data(Instruction));  // open: sel

  // Notes on the sheet:
  //   contents of rom_1 (hex, n*v repeats v):
  //   111 0 44
endmodule
